// Digital circuit B-Result.dig as structural Verilog
module B_Result (
  input  A,
  input  C,
  input  D,
  output Y
);

  wire and_1_out, and_2_out, not_1_out, not_2_out, not_3_out;

  not not_1 (not_1_out, A);
  not not_2 (not_2_out, C);
  not not_3 (not_3_out, D);
  and and_1 (and_1_out, not_1_out, not_2_out, D);
  and and_2 (and_2_out, A, not_2_out, not_3_out);
  or or_1 (Y, and_1_out, and_2_out);
endmodule
