// Digital circuit Branch.dig as structural Verilog
module Branch (
  input  A,
  input  B,
  input  C,
  input  D,
  input  E,
  input  F,
  input  G,
  output Y
);

  wire not_1_out, not_2_out, not_3_out;

  not not_1 (not_1_out, C);
  not not_2 (not_2_out, D);
  not not_3 (not_3_out, E);
  and and_1 (Y, A, B, not_1_out, not_2_out, not_3_out, F, G);
endmodule
