// Digital circuit ImmExt.dig as structural Verilog
module ImmExt (
  input  [16:0] IN,
  input  [2:0] funct3,
  input  [4:0] rs1,
  input  [1:0] ImmSrc,
  output [31:0] OUT
);

  wire [31:0] b_immext_1_out, i_immext_1_out, j_immext_1_out, s_immext_1_out;

  I_ImmExt i_immext_1 (.IN(IN), .OUT(i_immext_1_out));
  S_ImmExt s_immext_1 (.IN(IN), .OUT(s_immext_1_out));
  B_ImmExt b_immext_1 (.IN(IN), .OUT(b_immext_1_out));
  J_ImmExt j_immext_1 (.IN(IN), .funct3(funct3), .rs1(rs1), .OUT(j_immext_1_out));
  Multiplexer #(.Bits(32), .Selector_Bits(2)) multiplexer_1 (
    .sel(ImmSrc), .in_0(i_immext_1_out), .in_1(s_immext_1_out), .in_2(b_immext_1_out), .in_3(j_immext_1_out),
    .out(OUT));
endmodule
