// Digital circuit ImmSrc.dig as structural Verilog
module ImmSrc (
  input  A,
  input  B,
  input  C,
  input  D,
  input  E,
  input  F,
  input  G,
  output [1:0] out
);

  wire and_1_out, and_2_out, and_3_out, and_4_out, not_1_out, not_2_out, not_3_out, not_4_out;

  not not_1 (not_1_out, A);
  not not_2 (not_2_out, C);
  not not_3 (not_3_out, D);
  not not_4 (not_4_out, E);
  and and_1 (and_1_out, A, B, not_2_out, not_3_out, not_4_out, F, G);
  and and_2 (and_2_out, A, B, not_2_out, D, E, F, G);
  and and_3 (and_3_out, not_1_out, B, not_2_out, not_3_out, not_4_out, F, G);
  and and_4 (and_4_out, A, B, not_2_out, D, E, F, G);
  or or_1 (out[1], and_1_out, and_2_out);
  or or_2 (out[0], and_3_out, and_4_out);
endmodule
