// Digital circuit J-ImmExt.dig as structural Verilog
module J_ImmExt (
  input  [16:0] IN,
  input  [2:0] funct3,
  input  [4:0] rs1,
  output [31:0] OUT
);


  assign OUT = {{12{1'b0}}, rs1, funct3, IN[5], IN[15:6], 1'b0};
endmodule
