// Digital circuit JalSrc.dig as structural Verilog
module JalSrc (
  input  A,
  input  B,
  input  C,
  input  D,
  input  E,
  input  F,
  input  G,
  output Y
);

  wire not_1_out;

  not not_1 (not_1_out, C);
  and and_1 (Y, A, B, not_1_out, D, E, F, G);
endmodule
