// Digital circuit Jump.dig as structural Verilog
module Jump (
  input  A,
  input  B,
  input  C,
  input  E,
  input  F,
  input  G,
  output Y
);

  wire not_1_out;

  not not_1 (not_1_out, C);
  and and_1 (Y, A, B, not_1_out, E, F, G);
endmodule
