// Digital circuit MemWrite.dig as structural Verilog
module MemWrite (
  input  A,
  input  B,
  input  C,
  input  D,
  input  E,
  input  F,
  input  G,
  output Y
);

  wire not_1_out, not_2_out, not_3_out, not_4_out;

  not not_1 (not_1_out, A);
  not not_2 (not_2_out, C);
  not not_3 (not_3_out, D);
  not not_4 (not_4_out, E);
  and and_1 (Y, not_1_out, B, not_2_out, not_3_out, not_4_out, F, G);
endmodule
