// Digital circuit ResultSrc.dig as structural Verilog
module ResultSrc (
  input  A,
  input  B,
  input  C,
  input  D,
  input  E,
  input  F,
  input  G,
  output [1:0] out
);

  wire not_1_out, not_2_out, not_3_out, not_4_out, not_5_out;

  not not_1 (not_1_out, A);
  not not_2 (not_2_out, B);
  not not_3 (not_3_out, C);
  not not_4 (not_4_out, D);
  not not_5 (not_5_out, E);
  and and_1 (out[1], A, B, not_3_out, E, F, G);
  and and_2 (out[0], not_1_out, not_2_out, not_3_out, not_4_out, not_5_out, F, G);
endmodule
