// Digital circuit UC.dig as structural Verilog
module UC (
  input  [6:0] OPcode,
  input  [2:0] Funct3,
  input  [6:0] Funct7,
  input  [31:0] ULAResult,
  input  [4:0] rd,
  output PCSrc,
  output RegWrite,
  output [1:0] ImmSrc,
  output ULASrc,
  output MemWrite,
  output [1:0] ResultSrc,
  output [2:0] ULAControl,
  output JalSrc
);

  wire and_2_out, b_result_1_y, branch_1_p1, jump_1_p1, regwrite_1_p1, x0_block_1_out;
  wire [1:0] ulaop_1_p3;

  B_Result b_result_1 (.A(ULAResult[0]), .C(Funct3[1]), .D(Funct3[0]), .Y(b_result_1_y));
  // Branch branch_1: pin names not known; wires that end beside it: branch_1_p1
  // Jump jump_1: pin names not known; wires that end beside it: jump_1_p1
  // RegWrite regwrite_1: pin names not known; wires that end beside it: regwrite_1_p1, ImmSrc
  x0_block x0_block_1 (.IN(rd), .OUT(x0_block_1_out));
  ImmSrc immsrc_1 (
    .A(OPcode[6]), .B(OPcode[5]), .C(OPcode[4]), .D(OPcode[3]), .E(OPcode[2]), .F(OPcode[1]), .G(OPcode[0]));  // open: out
  and and_1 (RegWrite, regwrite_1_p1, x0_block_1_out);
  and and_2 (and_2_out, b_result_1_y, branch_1_p1);
  or or_1 (PCSrc, and_2_out, jump_1_p1);
  ULASrc ulasrc_1 (
    .A(OPcode[6]), .B(OPcode[5]), .C(OPcode[4]), .D(OPcode[3]), .E(OPcode[2]), .F(OPcode[1]), .G(OPcode[0]));  // open: Y
  MemWrite memwrite_1 (
    .A(OPcode[6]), .B(OPcode[5]), .C(OPcode[4]), .D(OPcode[3]), .E(OPcode[2]), .F(OPcode[1]), .G(OPcode[0]));  // open: Y
  ResultSrc resultsrc_1 (
    .A(OPcode[6]), .B(OPcode[5]), .C(OPcode[4]), .D(OPcode[3]), .E(OPcode[2]), .F(OPcode[1]), .G(OPcode[0]));  // open: out
  // ULAOp ulaop_1: pin names not known; wires that end beside it: MemWrite, ResultSrc, ulaop_1_p3, JalSrc
  JalSrc jalsrc_1 (
    .A(OPcode[6]), .B(OPcode[5]), .C(OPcode[4]), .D(OPcode[3]), .E(OPcode[2]), .F(OPcode[1]), .G(OPcode[0]));  // open: Y
  ULAControl ulacontrol_1 (
    .A(ulaop_1_p3[1]), .B(ulaop_1_p3[0]), .C(Funct7[5]), .D(Funct3[2]), .E(Funct3[1]), .F(Funct3[0]),
    .OUT(ULAControl));

  // Other names for the same wires on the sheet: in[6:0] = OPcode
endmodule
