// Digital circuit ULA.dig as structural Verilog
module ULA (
  input  [31:0] A,
  input  [2:0] FUNC,
  input  [31:0] B,
  output [31:0] R
);

  wire comparator_1_eq, comparator_1_lt;
  wire [31:0] add_1_s, add_2_s, and_1_out, barrelshifter_1_out, bitextender_1_out, bitextender_2_out,
       multiplexer_1_out, not_1_out, or_1_out, xor_1_out;

  Multiplexer #(.Bits(32)) multiplexer_1 (.sel(FUNC[0]), .in_0(B), .in_1(not_1_out), .out(multiplexer_1_out));
  assign not_1_out = ~B;  // Not not_1, 32 bits wide
  Add #(.Bits(32)) add_1 (.a(A), .b(multiplexer_1_out), .c_i(1'b0), .s(add_1_s));  // open: c_o
  Add #(.Bits(32)) add_2 (.a(A), .b(multiplexer_1_out), .c_i(1'b1), .s(add_2_s));  // open: c_o
  assign xor_1_out = A ^ B;  // XOr xor_1, 32 bits wide
  assign or_1_out = A | B;  // Or or_1, 32 bits wide
  assign and_1_out = A & B;  // And and_1, 32 bits wide
  BarrelShifter #(.Bits(32)) barrelshifter_1 (.in(A), .shift(B[5:0]), .out(barrelshifter_1_out));
  Comparator #(.Bits(32)) comparator_1 (.a(A), .b(B), .eq(comparator_1_eq), .lt(comparator_1_lt));  // open: gt
  BitExtender #(.inputBits(1), .outputBits(32)) bitextender_1 (.in(comparator_1_eq), .out(bitextender_1_out));
  BitExtender #(.inputBits(1), .outputBits(32)) bitextender_2 (.in(comparator_1_lt), .out(bitextender_2_out));
  Multiplexer #(.Selector_Bits(3), .Bits(32)) multiplexer_2 (
    .sel(FUNC), .in_0(add_1_s), .in_1(add_2_s), .in_2(xor_1_out), .in_3(or_1_out), .in_4(and_1_out),
    .in_5(barrelshifter_1_out), .in_6(bitextender_1_out), .in_7(bitextender_2_out), .out(R));

  // Other names for the same wires on the sheet: ULAControl[2:0] = FUNC
endmodule
