// Digital circuit ULAControl.dig as structural Verilog
module ULAControl (
  input  A,
  input  B,
  input  C,
  input  D,
  input  E,
  input  F,
  output [2:0] OUT
);

  wire and_1_out, and_2_out, and_3_out, and_4_out, and_5_out, and_6_out, and_7_out, and_8_out, and_9_out,
       and_10_out, and_11_out, and_12_out, and_13_out, and_14_out, and_15_out, and_16_out, and_17_out,
       and_18_out, not_1_out, not_2_out, not_3_out, not_4_out, not_5_out, not_6_out;

  not not_1 (not_1_out, A);
  not not_2 (not_2_out, B);
  not not_3 (not_3_out, C);
  not not_4 (not_4_out, D);
  not not_5 (not_5_out, E);
  not not_6 (not_6_out, F);
  and and_1 (and_1_out, not_1_out, not_2_out, not_3_out, not_4_out, E, not_6_out);
  and and_2 (and_2_out, not_1_out, not_2_out, not_3_out, D, E, F);
  and and_3 (and_3_out, A, B, not_4_out, E, not_6_out);
  and and_4 (and_4_out, A, B, D, E, F);
  and and_5 (and_5_out, A, not_4_out, not_5_out, F);
  and and_6 (and_6_out, A, not_2_out, not_5_out);
  and and_7 (and_7_out, not_2_out, not_3_out, not_4_out, not_5_out, F);
  and and_8 (and_8_out, not_1_out, not_2_out, not_3_out, E, not_6_out);
  and and_9 (and_9_out, A, D, not_5_out, not_6_out);
  and and_10 (and_10_out, A, B, E, not_6_out);
  and and_11 (and_11_out, A, not_2_out, not_5_out);
  and and_12 (and_12_out, not_2_out, not_3_out, D, not_5_out, not_6_out);
  and and_13 (and_13_out, not_1_out, not_2_out, not_3_out, not_4_out, not_5_out, F);
  and and_14 (and_14_out, not_1_out, not_2_out, C, not_4_out, not_5_out, not_6_out);
  and and_15 (and_15_out, A, B, not_4_out, not_5_out, F);
  and and_16 (and_16_out, not_1_out, not_2_out, not_3_out, E, not_6_out);
  and and_17 (and_17_out, A, B, E, not_6_out);
  and and_18 (and_18_out, A, not_2_out, D, not_5_out);
  or or_1 (OUT[2], and_1_out, and_2_out, and_3_out, and_4_out, and_5_out, and_6_out, and_7_out);
  or or_2 (OUT[1], and_8_out, and_9_out, and_10_out, and_11_out, and_12_out);
  or or_3 (OUT[0], and_13_out, and_14_out, and_15_out, and_16_out, and_17_out, and_18_out);

  // Other names for the same wires on the sheet: OUT_0 = OUT[0]; OUT_1 = OUT[1]; OUT_2 = OUT[2]
endmodule
