// Digital circuit main.dig as structural Verilog
module main (
  input  clk
);

  wire halt_1_out, JalSrc, MemWrite, PCSrc, RegWrite, ULASrc;
  wire [1:0] ImmSrc, ResultSrc;
  wire [2:0] PC_d_3, ULAControl;
  wire [4:0] PC_d_4;
  wire [6:0] PC_d;
  wire [16:0] PC_d_2;
  wire [23:0] add_1_s, add_2_s, multiplexer_1_out, register_1_q, ula_1_r;
  wire [31:0] Banco_de_registradores_da, Banco_de_registradores_db, immext_1_out, multiplexer_2_out,
       multiplexer_3_out, multiplexer_4_out, ramdualport_1_d;
  wire [31:24] add_2_s_2, ula_1_r_2;

  Multiplexer #(.Bits(24)) multiplexer_1 (.sel(PCSrc), .in_0(add_1_s), .in_1(add_2_s), .out(multiplexer_1_out));
  HALT halt_1 (.IN({PC_d_2[16:5], PC_d_4, PC_d_3, PC_d_2[4:0], PC_d}), .OUT(halt_1_out));
  Register #(.Bits(24)) register_1 (.D(multiplexer_1_out), .C(clk), .en(1'b1), .Q(register_1_q));
  Stop stop_1 (.stop(halt_1_out));
  Add #(.Bits(24)) add_1 (.a(register_1_q), .b(24'h4), .c_i(1'b0), .s(add_1_s));  // open: c_o
  ROM #(.AddrBits(24), .Bits(32)) PC (
    .A(register_1_q), .sel(1'b1), .D({PC_d_2[16:5], PC_d_4, PC_d_3, PC_d_2[4:0], PC_d}));
  UC uc_1 (
    .OPcode(PC_d), .Funct3(PC_d_3), .Funct7(PC_d_2[16:10]), .ULAResult({ula_1_r_2, ula_1_r}),
    .rd(PC_d_2[4:0]), .PCSrc(PCSrc), .RegWrite(RegWrite), .ImmSrc(ImmSrc), .ULASrc(ULASrc),
    .MemWrite(MemWrite), .ResultSrc(ResultSrc), .ULAControl(ULAControl), .JalSrc(JalSrc));
  RegisterFile #(.AddrBits(5), .Bits(32)) Banco_de_registradores (
    .Din(multiplexer_4_out), .we(RegWrite), .Rw(PC_d_2[4:0]), .C(clk), .Ra(PC_d_4), .Rb(PC_d_2[9:5]),
    .Da(Banco_de_registradores_da), .Db(Banco_de_registradores_db));
  ImmExt immext_1 (.IN(PC_d_2), .funct3(PC_d_3), .rs1(PC_d_4), .ImmSrc(ImmSrc), .OUT(immext_1_out));
  // Probe on immext_1_out
  Multiplexer #(.Bits(32)) multiplexer_2 (
    .sel(ULASrc), .in_0(Banco_de_registradores_db), .in_1(immext_1_out), .out(multiplexer_2_out));
  ULA ula_1 (.A(Banco_de_registradores_da), .FUNC(ULAControl), .B(multiplexer_2_out), .R({ula_1_r_2, ula_1_r}));
  Multiplexer #(.Bits(32)) multiplexer_3 (
    .sel(JalSrc), .in_0(Banco_de_registradores_da), .in_1({{8{1'b0}}, register_1_q}), .out(multiplexer_3_out));
  Add #(.Bits(32)) add_2 (.a(multiplexer_3_out), .b(immext_1_out), .c_i(1'b0), .s({add_2_s_2, add_2_s}));  // open: c_o
  RAMDualPort #(.AddrBits(24), .Bits(32)) ramdualport_1 (
    .A(ula_1_r), .Din(Banco_de_registradores_db), .str(MemWrite), .C(clk), .ld(1'b1), .D(ramdualport_1_d));
  Multiplexer #(.Selector_Bits(2), .Bits(32)) multiplexer_4 (
    .sel(ResultSrc), .in_0({ula_1_r_2, ula_1_r}), .in_1(ramdualport_1_d), .in_2({{8{1'b0}}, add_1_s}),
    .in_3({32{1'b0}}), .out(multiplexer_4_out));

  // Other names for the same wires on the sheet: C = clk

  // Notes on the sheet:
  //   clk: Hz: 15
  //   contents of PC (hex, n*v repeats v):
  //   1400393,0,0,0,428313,0,0,0,100513,0,0,0,100593,0,0,0,a2a023,0,0,0
  //   ,b32023,0,0,0,200e13,0,0,0,400eef,0,0,0,27e5263,0,0,0,2a503,0,0,0
  //   ,32583,0,0,0,428293,0,0,0,430313,0,0,0,b50533,0,0,0,a32023,0,0,0
  //   ,1e0e13,0,0,0,e80e7
endmodule
